# Fritzing sketch thermrf (saved by Fritzing 0.7.10b)
breadboards: 1

parts:
  IC1 = DS1302 [package="DIP8 [THT]"]
  Arduino1 = Arduino
  R1 = Resistor [tolerance=±5% resistance=1k package=THT]
  R2 = Resistor [tolerance=±5% resistance=1k package=THT]  # not connected
  R3 = Resistor [tolerance=±5% resistance=1k package=THT]

nets:
  N1: IC1.+V, Arduino1.A4, R1.Pin_1
  N2: IC1.X1_-_Crystal, Arduino1.A5, R3.Pin_1
  N3: IC1.0V, IC1.CE_-_Chip_Enable, IC1.I/O_-_SPI_Data_In/Out, IC1.SCLK_-_SPI_Clock, Arduino1.GND
  N4: IC1.Vbat_-_Backup_Supply, Arduino1.+5V, R1.Pin_0, R3.Pin_0
